# Fritzing sketch Atmega329p3V3 (saved by Fritzing 0.9.1b)
breadboards: 1

parts:
  Raspberry_Pi1 = Raspberry Pi B rev2
  U1 = atmega328 [package=dip]
  LED1 = smd LED [color="Red (633nm)" package="0805 [SMD]"]

nets:
  3V3: Raspberry_Pi1.3V3, U1.VCC, U1.AVCC
  N1: Raspberry_Pi1.GPIO_14, U1.D0_(RX)
  N2: Raspberry_Pi1.GPIO_15, U1.D1_(TX)
  N3: Raspberry_Pi1.GPIO_18, U1.RESET
  GND: Raspberry_Pi1.GND, U1.GND, LED1.anode
  N4: U1.D13, LED1.cathode
