# Fritzing sketch UnoR3 (saved by Fritzing 0.9.1b)

parts:
  Raspberry_Pi1 = Raspberry Pi B rev2
  Bauteil1 = Arduino Uno (Rev3)
  Bauteil2 = Logic Level Converter

nets:
  N1: Raspberry_Pi1.3V3, Bauteil2.LV
  5V: Raspberry_Pi1.5V, Bauteil1.VIN
  GND: Raspberry_Pi1.GND, Bauteil1.GND, Bauteil2.GND
  N2: Raspberry_Pi1.GPIO_14, Bauteil2.TX_LV
  N3: Raspberry_Pi1.GPIO_15, Bauteil2.RX_LV
  N4: Raspberry_Pi1.GPIO_18, Bauteil2.TX2_LV
  N5: Bauteil1.D0/RX, Bauteil2.TX_HV
  N6: Bauteil1.D1/TX, Bauteil2.RX_HV
  N7: Bauteil1.RESET, Bauteil2.TX2_HV
  N8: Bauteil1.5V, Bauteil2.HV

notes:
  Connect these pins with a jumper!
